// Logisim project 4bitSubstractor.circ as structural Verilog: 1 circuit, main circuit main
module main (
  input  V
);

  wire and_1_out, and_2_out, and_3_out, clock_1_out, nq1_out, nq2_out, nq3_out;
  wire [3:0] T1_q;

  Clock clock_1 (.out(clock_1_out));
  not nq3 (nq3_out, T1_q[2]);
  not nq2 (nq2_out, T1_q[1]);
  not nq1 (nq1_out, T1_q[0]);
  and and_1 (and_1_out, nq3_out, nq1_out, nq2_out, V);
  and and_2 (and_2_out, nq2_out, nq1_out, V);
  and and_3 (and_3_out, nq1_out, V);
  T_Flip_Flop T4 (.clk(clock_1_out), .T(and_1_out), .Q(T1_q[3]));  // open: Qn, preset, reset, en
  T_Flip_Flop T3 (.clk(clock_1_out), .T(and_2_out), .Q(T1_q[2]));  // open: Qn, preset, reset, en
  T_Flip_Flop T2 (.clk(clock_1_out), .T(and_3_out), .Q(T1_q[1]));  // open: Qn, preset, reset, en
  T_Flip_Flop T1 (.clk(clock_1_out), .T(V), .Q(T1_q[0]));  // open: Qn, preset, reset, en
  // Probe on T1_q

  // Notes on the sheet:
  //   q4
  //   q2
  //   q3
  //   q1
  //   v
endmodule
